# Fritzing sketch sensors Sketch (saved by Fritzing 0.9.3b)
breadboards: 1

parts:
  Raspberry_Pi_Zero1 = Raspberry Pi Zero
  AM1 = AM2302 Humidity and Temperature Sensor
  Bauteil1 = Adafruit ADS1115 16Bit I2C ADC [part_number="Adafruit #1085"]
  Bauteil2 = MQ-7 breakout
  e-Paper-Driver-HAT1 = Universal e-Paper Raw Panel Driver HAT

nets:
  3V3: Raspberry_Pi_Zero1.3v3, Raspberry_Pi_Zero1.3V3, Bauteil1.VDD, e-Paper-Driver-HAT1.VCC
  N1: Raspberry_Pi_Zero1.GPIO2, Bauteil1.SDA
  N2: Raspberry_Pi_Zero1.GPIO3, Bauteil1.SCL
  GND: Raspberry_Pi_Zero1.GND, AM1.GND, Bauteil1.GND, Bauteil2.GND, e-Paper-Driver-HAT1.GND
  N3: Raspberry_Pi_Zero1.GPIO17, e-Paper-Driver-HAT1.RST
  N4: Raspberry_Pi_Zero1.GPIO27, AM1.DATA
  N5: Raspberry_Pi_Zero1.GPIO10, e-Paper-Driver-HAT1.DIN
  N6: Raspberry_Pi_Zero1.GPIO11, e-Paper-Driver-HAT1.CLK
  N7: Raspberry_Pi_Zero1.GPIO8, e-Paper-Driver-HAT1.CS
  N8: Raspberry_Pi_Zero1.GPIO25, e-Paper-Driver-HAT1.DC
  N9: Raspberry_Pi_Zero1.GPIO24, e-Paper-Driver-HAT1.BUSY
  5V: Raspberry_Pi_Zero1.5V, AM1.VDD, Bauteil2.VCC
  N10: Bauteil1.AIN0, Bauteil2.AO

custom parts:
  Adafruit ADS1115 16Bit I2C ADC: For microcontrollers without an analog-to-digital converter or when you want a higher-precision ADC, the ADS1115 provides 16-bit precision at 860 samples/second over I2C. The chip can be configured as 4 single-ended input channels, or two differential channels. As a nice bonus, it even includes a programmable gain amplifier, up to x16, to help boost up smaller single/differential signals to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
  MQ-7 breakout: SKU: 101282
  Universal e-Paper Raw Panel Driver HAT: Universal e-Paper Driver HAT, supports various Waveshare SPI e-Paper raw panels
